# Fritzing sketch wiring-diagram (saved by Fritzing 0.9.6b)

parts:
  8_Channel_Relay1 = 8 Channel Power Relay
  J2 = Camdenboss CTB0158-9 [part_number=CTB0158-9 package=THT]
  M1 = AC-05-03
  J3 = Camdenboss CTB0158-9 [part_number=CTB0158-9 package=THT]
  J4 = Camdenboss CTB0158-9 [part_number=CTB0158-9 package=THT]
  J5 = Camdenboss CTB0158-9 [part_number=CTB0158-9 package=THT]
  U1 = ESP32-38PinWide [part_number=ESP32-38PinWide]

nets:
  N1: 8_Channel_Relay1.GND, J2.terminal_1
  N2: 8_Channel_Relay1.IN1, U1.GPIO18
  N3: 8_Channel_Relay1.IN2, U1.GPIO19
  N4: 8_Channel_Relay1.IN3, U1.GPIO21
  N5: 8_Channel_Relay1.IN4, U1.GPIO22
  N6: 8_Channel_Relay1.IN5, U1.GPIO23
  N7: 8_Channel_Relay1.IN6, U1.GPIO25
  N8: 8_Channel_Relay1.IN7, U1.GPIO26
  N9: 8_Channel_Relay1.IN8, U1.GPIO27
  N10: 8_Channel_Relay1.VCC#17, J4.terminal_9
  N11: 8_Channel_Relay1.VCC#19, 8_Channel_Relay1.JD-VCC
  N12: 8_Channel_Relay1.COM, J5.terminal_9
  N13: J2.terminal_9, M1.pin_5
  N14: M1.pin_1, J5.terminal_1
  N15: M1.pin_2, J3.terminal_9
  N16: M1.pin_4, J4.terminal_1

notes:
  AC
  Zone1
  Zone2
  Zone3
  Zone4
  Zone5
  Zone6
  Zone7
  Zone8

custom parts:
  8 Channel Power Relay: An 8 channel power relay. The module operates at 5V.
  AC-05-03: AC-DC 220V to 5V Step-Down Power Supply Module
  ESP32-38PinWide: Generic 38-Pin ESP32 with wide format (only access to one side of pins on a breadboard) based on Stephen Lilley's HiLetgo ESP-WROOM-32 ESP32 ESP-32S Development Board.
